# Fritzing sketch sensors (saved by Fritzing 0.9.9b)
breadboards: 1

parts:
  MCU1 = Raspberry Pi Zero
  Part3 = FC-28 Soil Hygrometer Module - Probe
  Part7 = FC-28 Soil Hygrometer Module - Probe
  Part8 = FC-28 Soil Hygrometer Module
  Part2 = FC-28 Soil Hygrometer Module

nets:
  VCC: MCU1.pin_1, MCU1.pin_17, Part8.VCC, Part2.VCC
  GND: MCU1.pin_9, MCU1.pin_25, MCU1.pin_34, Part8.GND, Part2.GND
  N1: MCU1.pin_11, Part2.DO
  N2: MCU1.pin_23, Part8.DO
  N3: Part3.POS, Part2.POS
  N4: Part3.NEG, Part2.NEG
  N5: Part7.POS, Part8.POS
  N6: Part7.NEG, Part8.NEG

custom parts:
  FC-28 Soil Hygrometer Module - Probe: The FC-28 is a soil hygrometer module that uses the Texas Instruments LM393 comparator chip to provide an analog measurement of soil humidity.
  FC-28 Soil Hygrometer Module: The FC-28 is a soil hygrometer module that uses the Texas Instruments LM393 comparator chip to provide an analog measurement of soil humidity. The digital output is high when soil moisture is over a certain threshold, as determined by adjusting the potentiometer.
