# Fritzing sketch servo (saved by Fritzing 0.9.9b)

parts:
  MCU2 = Raspberry Pi Zero
  KY-1 = Keyes Relay [package=THT]
  L1 = Solenoid  # not connected
  VCC1 = Battery block 9V

nets:
  N1: MCU2.pin_1, KY-1.power
  N2: MCU2.pin_7, KY-1.signal
  N3: MCU2.pin_9, KY-1.ground
  N4: KY-1.C, VCC1.-

custom parts:
  Keyes Relay: The Keyes 5V relay module is suitable for SCM development, home appliance control. It uses a 5V~12V TIL control signal which can control DC / AC signal.
